# Fritzing sketch Sketch_bot (saved by Fritzing 0.9.2b)
breadboards: 1

parts:
  IC1 = L293D [package=THT]
  M1 = DC Motor
  M2 = DC Motor
  VCC1 = 4 x AAA Battery Mount
  Raspberry_Pi1 = Raspberry Pi 2

nets:
  N1: IC1.Enable_1, Raspberry_Pi1.GPIO17
  N2: IC1.In_1, Raspberry_Pi1.GPIO18
  N3: IC1.Out_1_(_Controlled_by_Enable_1_), M1.pin_2
  N4: IC1.0V, VCC1.-
  N5: IC1.Out_2_(_Controlled_by_Enable_1_), M1.pin_1
  N6: IC1.In_2, Raspberry_Pi1.GPIO27
  N7: IC1.+Vmotor, IC1.+V, VCC1.+
  N8: IC1.Enable_2, Raspberry_Pi1.GPIO22
  N9: IC1.In_3, Raspberry_Pi1.GPIO23
  N10: IC1.Out_3_(_Controlled_by_Enable_2_), M2.pin_2
  N11: IC1.Out_4_(_Controlled_by_Enable_2_), M2.pin_1
  N12: IC1.In_4, Raspberry_Pi1.GPIO24
